# Fritzing sketch smokelamp_attiny84 (saved by Fritzing 0.9.3b)
circuit board: 5.118cm x 3.29492cm
breadboards: 2

parts:
  U1 = Voltage Regulator - 5V [package="TO220 [THT]"]
  IC1 = IC, DIP package, 14 pins [chip_label=IC]
  Q1 = Basic FET P-Channel [package="TO220 [THT]"]
  Q2 = Basic FET P-Channel [package="TO220 [THT]"]
  Q3 = Basic FET P-Channel [package="TO220 [THT]"]
  J1 = female pin header, 2 pins [form="♀ (female)"]
  R1 = Resistor [tolerance=±5% resistance=2.2k package=THT]
  R2 = Resistor [tolerance=±5% resistance=2.2k package=THT]
  R3 = Resistor [tolerance=±5% resistance=2.2k package=THT]
  J2 = female pin header, 2 pins [form="♀ (female)"]
  J3 = female pin header, 2 pins [form="♀ (female)"]
  J4 = female pin header, 2 pins [form="♀ (female)"]
  D1 = Rectifier Diode [part_number=1N4001 package="300 mil [THT]"]
  D2 = Rectifier Diode [part_number=1N4001 package="300 mil [THT]"]
  D3 = Rectifier Diode [part_number=1N4001 package="300 mil [THT]"]
  J5 = female pin header, 3 pins [form="♀ (female)"]
  R4 = Resistor [tolerance=±5% resistance=220 package=THT]

nets:
  N1: U1.input_voltage, J1.pin2, J2.pin1, J3.pin1, J4.pin1, D1.cathode, D2.cathode, D3.cathode
  N2: U1.GND, IC1.pin14, Q1.source, Q2.source, Q3.source, J1.pin1, J5.pin2
  N3: U1.output_voltage, IC1.pin1, J5.pin1, R4.Pin_0
  N4: IC1.pin5, R3.Pin_1
  N5: IC1.pin6, R1.Pin_1
  N6: IC1.pin7, R2.Pin_1
  N7: IC1.pin8, J5.pin3, R4.Pin_1
  N8: Q1.gate, R2.Pin_0
  N9: Q1.drain, J4.pin2, D3.anode
  N10: Q2.gate, R1.Pin_0
  N11: Q2.drain, J3.pin2, D2.anode
  N12: Q3.gate, R3.Pin_0
  N13: Q3.drain, J2.pin2, D1.anode
